# Fritzing sketch potentiometer_Servo (saved by Fritzing 0.9.3b)
breadboards: 1

parts:
  A1 = Arduino UNO R4 WiFi
  R3 = Trimmer Potentiometer [maximum_resistance=10kΩ package=THT]
  J1 = Basic Servo

nets:
  N1: A1.Pin_2, A1.Pin_48, R3.leg2, J1.gnd
  N2: A1.Pin_8, R3.leg1, J1.vcc
  N3: A1.Pin_12, R3.wiper

custom parts:
  Arduino UNO R4 WiFi: The Arduino UNO R4 WiFi merges the RA4M1 microprocessor from Renesas with the ESP32-S3 from Espressif, creating an all-in-one tool for makers with enhanced processing power and a diverse array of new peripherals.
